# Fritzing sketch Push Button Start (saved by Fritzing 0.9.3b)
breadboards: 1

parts:
  LED1 = LED - 5mm [color="Red (633nm)" package="5 mm [THT]"]
  S1 = Pushbutton [package="[THT]"]
  U1 = 4-Channel 5v Relay Shield [package=relay-4ch5v10a]
  Part1 = Adafruit Metro Mini [part_number="Adafruit #2590"]
  R1 = Resistor [tolerance=±5% resistance=220 package=THT]
  S2 = Toggle Switch [package=THT]
  Q2 = Basic FET N-Channel [package="TO220 [THT]"]
  ENCODER1 = Rotary Encoder with Knob [part_number="Ignition Switch"]
  BAT1 = Battery Holders [part_number="12V Automotive" package=battery]
  S3 = Toggle Switch [package=THT]

nets (from the breadboard view):
  N1: LED1.cathode, Q2.drain
  N2: LED1.anode, U1.K1-Off, U1.K2-Off, U1.K3-Off, U1.K4-Off, Part1.VIN, ENCODER1.no_name_yet#3, ENCODER1.no_name_yet#5, BAT1.+
  GND: S1.Pin_1, S1.Pin_2, U1.GND, Part1.GND, S2.L2, Q2.source, BAT1.-, S3.L2
  N3: S1.Pin_3, S1.Pin_4, Part1.IO2
  VCC: U1.VCC, Part1.+5V
  N4: U1.IN1, Part1.IO5
  N5: U1.IN2, Part1.IO6
  N6: U1.K1-In, ENCODER1.no_name_yet#1
  N7: U1.K2-In, ENCODER1.no_name_yet#2
  N8: U1.IN4, Part1.IO8
  N9: U1.K3-In, ENCODER1.no_name_yet#4
  N10: U1.IN3, Part1.IO7
  N11: Part1.IO9, R1.Pin_0
  N12: Part1.IO4, S3.L1
  N13: Part1.IO3, S2.L1
  N14: R1.Pin_1, Q2.gate

notes:
  killswitch (brake)
  4ch Relay Board
  push start
  Vin - 12V
  killswitch (alarm, nfc, etc)
  start
  Vin - 12v
  ign
  acc
  Piggy back to existing ignition switch wiring
  ignition switch
  killswitch (allarm, nfc, etc)
  piggy back on existing ign switch wires
  12V batt
  12V Automotive Battery

custom parts:
  4-Channel 5v Relay Shield: 4 Channel 5v Relay Shield w. 2x SPD-06VDC-SD-C
  Adafruit Metro Mini: We sure love the ATmega328 here at Adafruit, and we use them a lot for our own projects. The processor has plenty of GPIO, Analog inputs, hardware UART SPI and I2C, timers and PWM galore - just enough for most simple projects. When we need to go small, we use a Pro Trinket 3V or 5V, but if you want to have USB-to-Serial built in, we reach for an Adafruit METRO Mini. METRO Mini is the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
  Rotary Encoder with Knob: Rotary Encoder with 1/4" Shaft and Knob
